// Logisim project 1.6) Soustracteur 2 bits.circ as structural Verilog: 1 circuit, main circuit main
module main (
  input  a1,
  input  a0,
  input  b1,
  input  b0,
  output s2,
  output s1,
  output s0
);

  wire adder_2_cout;
  wire [1:0] adder_1_out, not_1_out;

  not not_1 (not_1_out[0], b0);
  not not_2 (not_1_out[1], b1);
  Adder #(.width(2)) adder_1 (.a(2'b01), .b(not_1_out), .out(adder_1_out));  // open: cin, cout
  Adder #(.width(2)) adder_2 (.a({a1, a0}), .b(adder_1_out), .out({s1, s0}), .cout(adder_2_cout));  // open: cin
  not not_3 (s2, adder_2_cout);

  // Notes on the sheet:
  //   moins
  //   C2
endmodule
